// Logisim project Sagui_vetorial.circ as structural Verilog: 12 circuits, main circuit main
module main (
);

  wire A_S, CLK, IM_S, MEM_S_WE, MEM_V_WE, PC_S, WB_S, WE_S, WE_V, Z;
  wire [1:0] multiplexer_2_out, multiplexer_3_out, multiplexer_4_out, multiplexer_5_out, multiplexer_6_out;
  wire [2:0] ULA_S;
  wire [3:0] OP, Programa_data;
  wire [7:0] adder_1_out, B, Dados_S_dout, Dados_V0_dout, Dados_V1_dout, Dados_V2_dout, Dados_V3_dout,
       IM_EXT, multiplexer_1_out, multiplexer_7_out, multiplexer_8_out, multiplexer_9_out,
       multiplexer_10_out, multiplexer_11_out, multiplexer_12_out, multiplexer_13_out, multiplexer_14_out,
       multiplexer_15_out, multiplexer_16_out, PC_q, SR_a, ULA_S_s, ULA_V0_s, ULA_V1_s, ULA_V2_s, ULA_V3_s,
       VR0_a, VR0_b, VR1_a, VR1_b, VR2_a, VR2_b, VR3_a, VR3_b;
  wire [10:10] Controle_data;

  Multiplexer #(.width(8)) multiplexer_1 (.in0(adder_1_out), .in1(B), .out(multiplexer_1_out), .sel(PC_S));
  ROM #(.addrWidth(4), .dataWidth(11)) Controle (
    .addr(OP), .data({Controle_data[10], WE_V, WE_S, IM_S, ULA_S, MEM_V_WE, MEM_S_WE, WB_S, A_S}));
  Clock clock_1 (.out(CLK));
  Register PC (.D(multiplexer_1_out), .en(1'b1), .clk(CLK), .Q(PC_q));  // open: clr
  ROM Programa (.addr(PC_q), .data({OP, Programa_data}));
  Adder adder_1 (.a(8'h1), .b(PC_q), .out(adder_1_out));  // open: cin, cout
  and and_1 (PC_S, Controle_data[10], Z);
  assign IM_EXT = {{4{Programa_data[3]}}, Programa_data};  // Bit_Extender bit_extender_1
  Multiplexer #(.width(2)) multiplexer_2 (.in0(Programa_data[3:2]), .in1(2'b01), .out(multiplexer_2_out), .sel(A_S));
  Multiplexer #(.width(2)) multiplexer_3 (.in0(Programa_data[3:2]), .in1(2'b01), .out(multiplexer_3_out), .sel(A_S));
  Multiplexer #(.width(2)) multiplexer_4 (.in0(Programa_data[3:2]), .in1(2'b01), .out(multiplexer_4_out), .sel(A_S));
  Multiplexer #(.width(2)) multiplexer_5 (.in0(Programa_data[3:2]), .in1(2'b01), .out(multiplexer_5_out), .sel(A_S));
  Multiplexer #(.width(2)) multiplexer_6 (.in0(Programa_data[3:2]), .in1(2'b01), .out(multiplexer_6_out), .sel(A_S));
  Banco_de_registradores_V0 VR0 (
    .WE(WE_V), .CLK(CLK), .End_a(multiplexer_2_out), .End_b(Programa_data[1:0]), .W(multiplexer_12_out),
    .A(VR0_a), .B(VR0_b));
  Banco_de_registradores_V1 VR1 (
    .WE(WE_V), .CLK(CLK), .End_a(multiplexer_3_out), .End_b(Programa_data[1:0]), .W(multiplexer_13_out),
    .A(VR1_a), .B(VR1_b));
  Banco_de_registradores_V2 VR2 (
    .WE(WE_V), .CLK(CLK), .End_a(multiplexer_4_out), .End_b(Programa_data[1:0]), .W(multiplexer_14_out),
    .A(VR2_a), .B(VR2_b));
  Banco_de_registradores_V3 VR3 (
    .WE(WE_V), .CLK(CLK), .End_a(multiplexer_5_out), .End_b(Programa_data[1:0]), .W(multiplexer_15_out),
    .A(VR3_a), .B(VR3_b));
  Banco_de_registradores_S SR (
    .WE(WE_S), .CLK(CLK), .End_a(multiplexer_6_out), .End_b(Programa_data[1:0]), .W(multiplexer_16_out),
    .A(SR_a), .B(B));
  Multiplexer #(.width(8)) multiplexer_7 (.in0(VR0_b), .in1(IM_EXT), .out(multiplexer_7_out), .sel(IM_S));
  Multiplexer #(.width(8)) multiplexer_8 (.in0(VR1_b), .in1(IM_EXT), .out(multiplexer_8_out), .sel(IM_S));
  Multiplexer #(.width(8)) multiplexer_9 (.in0(VR2_b), .in1(IM_EXT), .out(multiplexer_9_out), .sel(IM_S));
  Multiplexer #(.width(8)) multiplexer_10 (.in0(VR3_b), .in1(IM_EXT), .out(multiplexer_10_out), .sel(IM_S));
  Multiplexer #(.width(8)) multiplexer_11 (.in0(B), .in1(IM_EXT), .out(multiplexer_11_out), .sel(IM_S));
  ULA_Vetorial ULA_V0 (.A(VR0_a), .B(multiplexer_7_out), .ULA_E_S(ULA_S), .S(ULA_V0_s));
  ULA_Vetorial ULA_V1 (.A(VR1_a), .B(multiplexer_8_out), .ULA_E_S(ULA_S), .S(ULA_V1_s));
  ULA_Vetorial ULA_V2 (.A(VR2_a), .B(multiplexer_9_out), .ULA_E_S(ULA_S), .S(ULA_V2_s));
  ULA_Vetorial ULA_V3 (.A(VR3_a), .B(multiplexer_10_out), .ULA_E_S(ULA_S), .S(ULA_V3_s));
  ULA_Escalar u_ULA_S (.A(SR_a), .B(multiplexer_11_out), .ULA_E_S(ULA_S), .S(ULA_S_s), .Z(Z));
  RAM Dados_V0 (.addr(VR0_b), .we(MEM_V_WE), .oe(1'b1), .clk(CLK), .din(VR0_a), .dout(Dados_V0_dout));
  RAM Dados_V1 (.addr(VR1_b), .we(MEM_V_WE), .oe(1'b1), .clk(CLK), .din(VR1_a), .dout(Dados_V1_dout));
  RAM Dados_V2 (.addr(VR2_b), .we(MEM_V_WE), .oe(1'b1), .clk(CLK), .din(VR2_a), .dout(Dados_V2_dout));
  RAM Dados_V3 (.addr(VR3_b), .we(MEM_V_WE), .oe(1'b1), .clk(CLK), .din(VR3_a), .dout(Dados_V3_dout));
  RAM Dados_S (.addr(B), .we(MEM_S_WE), .oe(1'b1), .clk(CLK), .din(SR_a), .dout(Dados_S_dout));
  Multiplexer #(.width(8)) multiplexer_12 (.in0(ULA_V0_s), .in1(Dados_V0_dout), .out(multiplexer_12_out), .sel(WB_S));
  Multiplexer #(.width(8)) multiplexer_13 (.in0(ULA_V1_s), .in1(Dados_V1_dout), .out(multiplexer_13_out), .sel(WB_S));
  Multiplexer #(.width(8)) multiplexer_14 (.in0(ULA_V2_s), .in1(Dados_V2_dout), .out(multiplexer_14_out), .sel(WB_S));
  Multiplexer #(.width(8)) multiplexer_15 (.in0(ULA_V3_s), .in1(Dados_V3_dout), .out(multiplexer_15_out), .sel(WB_S));
  Multiplexer #(.width(8)) multiplexer_16 (.in0(ULA_S_s), .in1(Dados_S_dout), .out(multiplexer_16_out), .sel(WB_S));

  // Notes on the sheet:
  //   contents of Controle (hex, n*v repeats v):
  //   102 4 181 191 120 130 140 450 202 8 281 291 220 230 240 250
  //   contents of Programa (hex, n*v repeats v):
  //   35 49 66 35 21 4d 5e 1e 7 20 3d 71 21 b5 c9 e6 b5 a1 cd de 9e 87 f9 5f da df d5 20 31 4d 22 36 79 95
  //   c4 5b 21 3e 71
endmodule

module Deslocador_esq_main (
  input  [7:0] A,
  input  [7:0] B,
  output [7:0] S
);

  wire or_1_out;
  wire [7:0] shifter_1_out;

  Shifter shifter_1 (.in(A), .\dist (B[2:0]), .out(shifter_1_out));
  or or_1 (or_1_out, B[3], B[4], B[5], B[6], B[7]);
  Multiplexer #(.width(8)) multiplexer_1 (.in0(shifter_1_out), .in1({8{1'b0}}), .out(S), .sel(or_1_out));
endmodule

module Deslocador_dir_main (
  input  [7:0] A,
  input  [7:0] B,
  output [7:0] S
);

  wire or_1_out;
  wire [7:0] shifter_1_out;

  Shifter #(.shift("lr")) shifter_1 (.in(A), .\dist (B[2:0]), .out(shifter_1_out));
  or or_1 (or_1_out, B[3], B[4], B[5], B[6], B[7]);
  Multiplexer #(.width(8)) multiplexer_1 (.in0(shifter_1_out), .in1({8{1'b0}}), .out(S), .sel(or_1_out));
endmodule

module Concatenador_High (
  input  [7:0] A,
  input  [7:0] B,
  output [7:0] S
);


  assign S = {B[3:0], A[3:0]};
endmodule

module Concatenador_Low (
  input  [7:0] A,
  input  [7:0] B,
  output [7:0] S
);


  assign S = {A[7:4], B[3:0]};
endmodule

module ULA_Escalar (
  input  [7:0] A,
  input  [7:0] B,
  input  [2:0] ULA_E_S,
  output [7:0] S,
  output Z
);

  wire comparator_1_eq;
  wire [7:0] adder_1_out, and_1_out, bit_extender_1_out, Concat_high_s, Concat_low_s, subtractor_1_out;

  Comparator comparator_1 (.a(A), .b({8{1'b0}}), .eq(comparator_1_eq));  // open: gt, lt
  Concatenador_High Concat_high (.A(A), .B(B), .S(Concat_high_s));
  Concatenador_Low Concat_low (.A(A), .B(B), .S(Concat_low_s));
  Adder adder_1 (.a(A), .b(B), .out(adder_1_out));  // open: cin, cout
  Subtractor subtractor_1 (.a(A), .b(B), .out(subtractor_1_out));  // open: bin, bout
  assign and_1_out = A & B;  // AND_Gate and_1, 8 bits wide
  assign bit_extender_1_out = {{7{1'b0}}, comparator_1_eq};  // Bit_Extender bit_extender_1
  Multiplexer #(.select(3), .width(8)) multiplexer_1 (
    .in0(Concat_high_s), .in1(Concat_low_s), .in2(adder_1_out), .in3(subtractor_1_out), .in4(and_1_out),
    .in5(bit_extender_1_out), .out(S), .sel(ULA_E_S));  // open: in6, in7

  assign Z = S[0];
endmodule

module ULA_Vetorial (
  input  [7:0] A,
  input  [7:0] B,
  input  [2:0] ULA_E_S,
  output [7:0] S
);

  wire [7:0] adder_1_out, and_1_out, Concat_high_s, Concat_low_s, or_1_out, subtractor_1_out;

  Concatenador_High Concat_high (.A(A), .B(B), .S(Concat_high_s));
  Concatenador_Low Concat_low (.A(A), .B(B), .S(Concat_low_s));
  Adder adder_1 (.a(A), .b(B), .out(adder_1_out));  // open: cin, cout
  Subtractor subtractor_1 (.a(A), .b(B), .out(subtractor_1_out));  // open: bin, bout
  assign and_1_out = A & B;  // AND_Gate and_1, 8 bits wide
  assign or_1_out = A | B;  // OR_Gate or_1, 8 bits wide
  Multiplexer #(.select(3), .width(8)) multiplexer_1 (
    .in0(Concat_high_s), .in1(Concat_low_s), .in2(adder_1_out), .in3(subtractor_1_out), .in4(and_1_out),
    .in5(or_1_out), .out(S), .sel(ULA_E_S));  // open: in6, in7
endmodule

module Banco_de_registradores_S (
  input  WE,
  input  CLK,
  input  [1:0] End_a,
  input  [1:0] End_b,
  input  [7:0] W,
  output [7:0] A,
  output [7:0] B
);

  wire demultiplexer_1_out1, demultiplexer_1_out2, demultiplexer_1_out3;
  wire [7:0] register_1_q, register_2_q, register_3_q;

  Demultiplexer #(.select(2)) demultiplexer_1 (
    .out1(demultiplexer_1_out1), .out2(demultiplexer_1_out2), .out3(demultiplexer_1_out3), .in(WE),
    .sel(End_a));  // open: out0
  Register register_1 (.D(W), .en(demultiplexer_1_out2), .clk(CLK), .Q(register_1_q));  // open: clr
  Register register_2 (.D(W), .en(demultiplexer_1_out3), .clk(CLK), .Q(register_2_q));  // open: clr
  Register register_3 (.D(W), .en(demultiplexer_1_out1), .clk(CLK), .Q(register_3_q));  // open: clr
  Multiplexer #(.select(2), .width(8)) multiplexer_1 (
    .in0({8{1'b0}}), .in1(register_3_q), .in2(register_1_q), .in3(register_2_q), .out(A), .sel(End_a));
  Multiplexer #(.select(2), .width(8)) multiplexer_2 (
    .in0({8{1'b0}}), .in1(register_3_q), .in2(register_1_q), .in3(register_2_q), .out(B), .sel(End_b));
endmodule

module Banco_de_registradores_V0 (
  input  WE,
  input  CLK,
  input  [1:0] End_a,
  input  [1:0] End_b,
  input  [7:0] W,
  output [7:0] A,
  output [7:0] B
);

  wire demultiplexer_1_out1, demultiplexer_1_out2, demultiplexer_1_out3;
  wire [7:0] register_1_q, register_2_q, register_3_q;

  Demultiplexer #(.select(2)) demultiplexer_1 (
    .out1(demultiplexer_1_out1), .out2(demultiplexer_1_out2), .out3(demultiplexer_1_out3), .in(WE),
    .sel(End_a));  // open: out0
  Register register_1 (.D(W), .en(demultiplexer_1_out2), .clk(CLK), .Q(register_1_q));  // open: clr
  Register register_2 (.D(W), .en(demultiplexer_1_out3), .clk(CLK), .Q(register_2_q));  // open: clr
  Register register_3 (.D(W), .en(demultiplexer_1_out1), .clk(CLK), .Q(register_3_q));  // open: clr
  Multiplexer #(.select(2), .width(8)) multiplexer_1 (
    .in0({8{1'b0}}), .in1(register_3_q), .in2(register_1_q), .in3(register_2_q), .out(A), .sel(End_a));
  Multiplexer #(.select(2), .width(8)) multiplexer_2 (
    .in0({8{1'b0}}), .in1(register_3_q), .in2(register_1_q), .in3(register_2_q), .out(B), .sel(End_b));
endmodule

module Banco_de_registradores_V1 (
  input  WE,
  input  CLK,
  input  [1:0] End_a,
  input  [1:0] End_b,
  input  [7:0] W,
  output [7:0] A,
  output [7:0] B
);

  wire demultiplexer_1_out1, demultiplexer_1_out2, demultiplexer_1_out3;
  wire [7:0] register_1_q, register_2_q, register_3_q;

  Demultiplexer #(.select(2)) demultiplexer_1 (
    .out1(demultiplexer_1_out1), .out2(demultiplexer_1_out2), .out3(demultiplexer_1_out3), .in(WE),
    .sel(End_a));  // open: out0
  Register register_1 (.D(W), .en(demultiplexer_1_out2), .clk(CLK), .Q(register_1_q));  // open: clr
  Register register_2 (.D(W), .en(demultiplexer_1_out3), .clk(CLK), .Q(register_2_q));  // open: clr
  Register register_3 (.D(W), .en(demultiplexer_1_out1), .clk(CLK), .Q(register_3_q));  // open: clr
  Multiplexer #(.select(2), .width(8)) multiplexer_1 (
    .in0(8'h1), .in1(register_3_q), .in2(register_1_q), .in3(register_2_q), .out(A), .sel(End_a));
  Multiplexer #(.select(2), .width(8)) multiplexer_2 (
    .in0(8'h1), .in1(register_3_q), .in2(register_1_q), .in3(register_2_q), .out(B), .sel(End_b));
endmodule

module Banco_de_registradores_V2 (
  input  WE,
  input  CLK,
  input  [1:0] End_a,
  input  [1:0] End_b,
  input  [7:0] W,
  output [7:0] A,
  output [7:0] B
);

  wire demultiplexer_1_out1, demultiplexer_1_out2, demultiplexer_1_out3;
  wire [7:0] register_1_q, register_2_q, register_3_q;

  Demultiplexer #(.select(2)) demultiplexer_1 (
    .out1(demultiplexer_1_out1), .out2(demultiplexer_1_out2), .out3(demultiplexer_1_out3), .in(WE),
    .sel(End_a));  // open: out0
  Register register_1 (.D(W), .en(demultiplexer_1_out2), .clk(CLK), .Q(register_1_q));  // open: clr
  Register register_2 (.D(W), .en(demultiplexer_1_out3), .clk(CLK), .Q(register_2_q));  // open: clr
  Register register_3 (.D(W), .en(demultiplexer_1_out1), .clk(CLK), .Q(register_3_q));  // open: clr
  Multiplexer #(.select(2), .width(8)) multiplexer_1 (
    .in0(8'h2), .in1(register_3_q), .in2(register_1_q), .in3(register_2_q), .out(A), .sel(End_a));
  Multiplexer #(.select(2), .width(8)) multiplexer_2 (
    .in0(8'h2), .in1(register_3_q), .in2(register_1_q), .in3(register_2_q), .out(B), .sel(End_b));
endmodule

module Banco_de_registradores_V3 (
  input  WE,
  input  CLK,
  input  [1:0] End_a,
  input  [1:0] End_b,
  input  [7:0] W,
  output [7:0] A,
  output [7:0] B
);

  wire demultiplexer_1_out1, demultiplexer_1_out2, demultiplexer_1_out3;
  wire [7:0] register_1_q, register_2_q, register_3_q;

  Demultiplexer #(.select(2)) demultiplexer_1 (
    .out1(demultiplexer_1_out1), .out2(demultiplexer_1_out2), .out3(demultiplexer_1_out3), .in(WE),
    .sel(End_a));  // open: out0
  Register register_1 (.D(W), .en(demultiplexer_1_out2), .clk(CLK), .Q(register_1_q));  // open: clr
  Register register_2 (.D(W), .en(demultiplexer_1_out3), .clk(CLK), .Q(register_2_q));  // open: clr
  Register register_3 (.D(W), .en(demultiplexer_1_out1), .clk(CLK), .Q(register_3_q));  // open: clr
  Multiplexer #(.select(2), .width(8)) multiplexer_1 (
    .in0(8'h3), .in1(register_3_q), .in2(register_1_q), .in3(register_2_q), .out(A), .sel(End_a));
  Multiplexer #(.select(2), .width(8)) multiplexer_2 (
    .in0(8'h3), .in1(register_3_q), .in2(register_1_q), .in3(register_2_q), .out(B), .sel(End_b));
endmodule
